# Fritzing sketch Serial-Wifi-PCB (saved by Fritzing 0.9.3b)
circuit board: 7.6527cm x 2.68226cm
breadboards: 1

parts:
  Adafruit_HUZZAH_ESP8266 = Adafruit HUZZAH ESP8266 Breakout [part_number=2471]
  USB = USB+SHIELD [package=usb-b-pth]
  CTS/RTS = female pin header, 2 pins [form="♀ (female)"]
  G-Tx-Rx-V+ = female pin header, 4 pins [form="♀ (female)"]
  Pad1 = Pad [width=2 height=1 connect=center]
  Pad2 = Pad [width=2 height=1 connect=center]
  Pad3 = Pad [width=2 height=1 connect=center]
  Pad4 = Pad [width=2 height=1 connect=center]

nets:
  GND: Adafruit_HUZZAH_ESP8266.GND, USB.GND, G-Tx-Rx-V+.pin4, Pad3.pad, Pad4.pad
  N1: Adafruit_HUZZAH_ESP8266.TX, G-Tx-Rx-V+.pin2
  N2: Adafruit_HUZZAH_ESP8266.RX, G-Tx-Rx-V+.pin3
  N3: Adafruit_HUZZAH_ESP8266.V+, USB.VBUS, G-Tx-Rx-V+.pin1
  N4: CTS/RTS.pin1, Pad1.pad
  N5: CTS/RTS.pin2, Pad2.pad
